# Fritzing sketch wiring (saved by Fritzing 0.9.3b)

parts:
  Bauteil1 = Arduino Pro Mini (3.3V)
  Sende/Config-Taster = Momentary Switch [package=ksa_sealed_tac_switch]
  R1+R2 = Resistor [tolerance=±5% resistance=330 package=THT]
  U1 = CC1101 [part_number=CC1101]
  LED1 = DUO LED RG [package="5 mm [THT]"]
  R2 = Resistor [tolerance=±5% resistance=330 package=THT]
  R3 = Slide Potentiometer [maximum_resistance=100kΩ]

nets:
  N1: Bauteil1.GND, U1.2, R3.leg2
  N2: Bauteil1.VCC, U1.1
  N3: Bauteil1.A0, R3.wiper
  N4: Bauteil1.SCK, U1.4
  N5: Bauteil1.MISO, U1.5
  N6: Bauteil1.MOSI, U1.3
  N7: Bauteil1.D10, U1.8
  N8: Bauteil1.D8, Sende/Config-Taster.3
  N9: Bauteil1.D6, R3.leg1
  N10: Bauteil1.D5, R2.Pin_0
  N11: Bauteil1.D4, R1+R2.Pin_0
  N12: Bauteil1.D2, U1.7
  N13: Sende/Config-Taster.4, LED1.common_cathode
  N14: R1+R2.Pin_1, LED1.green_anode
  N15: LED1.red_anode, R2.Pin_1
